# Fritzing sketch tonnetzWandSchematic (saved by Fritzing 0.9.3b)
breadboards: 1

parts:
  TonnetzWand = Arduino Uno (Rev3)
  Radio_Transmitter = NRF24L01+ Breakout Board
  Wii_Nunchuk = IC, DIP package, 6 pins [chip_label=Nunchuk]
  WS2812_LED = IC, DIP package, 6 pins [chip_label="WS2812 LED"]
  WS2812_LED1 = IC, DIP package, 6 pins [chip_label="WS2812 LED"]

nets:
  N1: TonnetzWand.A4/SDA, Wii_Nunchuk.pin1
  N2: TonnetzWand.A5/SCL, Wii_Nunchuk.pin2
  N3: TonnetzWand.D8, Radio_Transmitter.CS
  N4: TonnetzWand.D11_PWM/MOSI, Radio_Transmitter.MOSI
  N5: TonnetzWand.D12/MISO, Radio_Transmitter.MISO
  N6: TonnetzWand.D13/SCK, Radio_Transmitter.SCK
  GND: TonnetzWand.GND, Radio_Transmitter.GND, WS2812_LED.pin2
  N7: TonnetzWand.D3_PWM, WS2812_LED.pin1
  N8: TonnetzWand.D7, Radio_Transmitter.CE
  3V3: TonnetzWand.3V3, Radio_Transmitter.VCC, Wii_Nunchuk.pin3, Wii_Nunchuk.pin6
  N9: TonnetzWand.5V, WS2812_LED.pin3
  N10: WS2812_LED.pin4, WS2812_LED1.pin3
  N11: WS2812_LED.pin5, WS2812_LED1.pin2
  N12: WS2812_LED.pin6, WS2812_LED1.pin1

notes:
  SDA
  SCL
  3.3V
  GND
  nc
  DIN
  Do
  +5v
